# Fritzing sketch cactus-layout (saved by Fritzing 0.9.2b)
breadboards: 1

parts:
  OLED_I2C1 = OLED 128x64 I2C Monochrome Display
  OLED_I2C2 = OLED 128x64 I2C Monochrome Display
  Part1 = Adafruit MPR121
  BATT1 = 4xAA Switchable Battery Pack w/Bare Wire

nets:
  VDD: OLED_I2C1.VDD, OLED_I2C2.VDD, Part1.VIN
  GND: OLED_I2C1.GND, OLED_I2C2.GND, Part1.GND, BATT1.NEG

notes:
  TEENSY 3.5:
  GND
  3.3V
  SDA (i2c data)
  SCL (i2c clock)
  VIN (3.6-6.0V)

custom parts:
  Adafruit MPR121: Add lots of touch sensors to your next microcontroller project with this easy-to-use 12-channel capacitive touch sensor breakout board, starring the MPR121. This chip can handle up to 12 individual touch pads. The MPR121 has support for only I2C, which can be implemented with nearly any microcontroller. You can select one of 4 addresses with the ADDR pin, for a total of 48 capacitive touch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
  4xAA Switchable Battery Pack w/Bare Wire: 4xAA Switchable Battery Pack with Bare Wire connection
